# Fritzing sketch kilRegulator_controlerSchematic (saved by Fritzing 0.9.3b)
circuit board: 12.0379cm x 7.19319cm
breadboards: 1

parts:
  Part2 = Adafruit MAX31856 Thermocouple Amp [part_number="Adafruit #3263"]
  KY-1 = Keyes Relay [package=THT]
  TFT_1_44_OLEd = IC, SIP package, 11 pins [chip_label="TFT 1.44\" OLED"]
  Part1 = Arduino Uno (Rev3)

nets:
  N1: Part2.!CS, Part1.D7
  N2: Part2.SDI, Part1.D4
  N3: Part2.SDO, Part1.D5_PWM
  N4: Part2.SCK, Part1.D3_PWM
  GND: Part2.GND, KY-1.ground, TFT_1_44_OLEd.pin3, Part1.GND
  N5: Part2.VIN, KY-1.power, TFT_1_44_OLEd.pin1, TFT_1_44_OLEd.pin6, Part1.ioref
  N6: KY-1.signal, Part1.D2
  N7: KY-1.NC, KY-1.C, KY-1.NO
  N8: TFT_1_44_OLEd.pin7, Part1.D13/SCK
  N9: TFT_1_44_OLEd.pin8, Part1.D11_PWM/MOSI
  N10: TFT_1_44_OLEd.pin9, Part1.D8
  N11: TFT_1_44_OLEd.pin10, Part1.D9_PWM
  N12: TFT_1_44_OLEd.pin11, Part1.D10_PWM/SS

custom parts:
  Adafruit MAX31856 Thermocouple Amp: Thermocouples are very sensitive, requiring a good amplifier with a cold-compensation reference, as well as calculations to handle any non-linearities. For a long time we've suggested our MAX31855K breakout, which works great but is only for K-type thermocouples. Now we're happy to offer a great new thermocouple amplifier/converter that can handle just about any type of thermocouple, and even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
  Keyes Relay: The Keyes 5V relay module is suitable for SCM development, home appliance control. It uses a 5V~12V TIL control signal which can control DC / AC signal.
