# Fritzing sketch kilRegulator_controlerSchematic_v2 (saved by Fritzing 0.9.3b)
circuit board: 13.2004cm x 6.00787cm
breadboards: 1

parts:
  Part2 = Adafruit MAX31856 Thermocouple Amp [part_number="Adafruit #3263"]
  TFT_1_44_OLEd = IC, SIP package, 11 pins [chip_label="TFT 1.44\" OLED"]
  Part1 = Arduino Uno (Rev3)
  U2 = 2-Channel 5v Relay Shield [package=relay-2ch5v10a]

nets:
  N1: Part2.!CS, Part1.D7
  N2: Part2.SDI, Part1.D4
  N3: Part2.SDO, Part1.D5_PWM
  N4: Part2.SCK, Part1.D3_PWM
  GND: Part2.GND, TFT_1_44_OLEd.pin3, Part1.GND, U2.GND
  VIN: Part2.VIN, TFT_1_44_OLEd.pin1, TFT_1_44_OLEd.pin6, Part1.ioref, U2.VCC
  N5: TFT_1_44_OLEd.pin7, Part1.D13/SCK
  N6: TFT_1_44_OLEd.pin8, Part1.D11_PWM/MOSI
  N7: TFT_1_44_OLEd.pin9, Part1.D8
  N8: TFT_1_44_OLEd.pin10, Part1.D9_PWM
  N9: TFT_1_44_OLEd.pin11, Part1.D10_PWM/SS
  N10: Part1.D2, U2.IN1

notes:
  the schematic is wrong but the breadboard and the PCB ok

custom parts:
  Adafruit MAX31856 Thermocouple Amp: Thermocouples are very sensitive, requiring a good amplifier with a cold-compensation reference, as well as calculations to handle any non-linearities. For a long time we've suggested our MAX31855K breakout, which works great but is only for K-type thermocouples. Now we're happy to offer a great new thermocouple amplifier/converter that can handle just about any type of thermocouple, and even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
  2-Channel 5v Relay Shield: 2 Channel 5v Relay Shield w. 2x SPD-06VDC-SD-C
