# Fritzing sketch kilRegulator_controlerSchematic_v3 (saved by Fritzing 0.9.3b)
circuit board: 10.7546cm x 6.84944cm
breadboards: 1

parts:
  Max31856 = Adafruit MAX31856 Thermocouple Amp [part_number="Adafruit #3263"]
  TFT_1_44_OLEd = IC, SIP package, 11 pins [chip_label="TFT 1.44\" OLED"]
  arduino_UNO = Arduino Uno (Rev3)
  Julien_Deantoni_2019 = 2-Channel 5v Relay Shield [package=relay-2ch5v10a]

nets:
  N1: Max31856.!CS, arduino_UNO.D7
  N2: Max31856.SDI, arduino_UNO.D4
  N3: Max31856.SDO, arduino_UNO.D5_PWM
  N4: Max31856.SCK, arduino_UNO.D3_PWM
  GND: Max31856.GND, TFT_1_44_OLEd.pin3, arduino_UNO.GND, Julien_Deantoni_2019.GND
  VIN: Max31856.VIN, TFT_1_44_OLEd.pin1, TFT_1_44_OLEd.pin6, arduino_UNO.ioref, Julien_Deantoni_2019.VCC
  N5: TFT_1_44_OLEd.pin7, arduino_UNO.D13/SCK
  N6: TFT_1_44_OLEd.pin8, arduino_UNO.D11_PWM/MOSI
  N7: TFT_1_44_OLEd.pin9, arduino_UNO.D8
  N8: TFT_1_44_OLEd.pin10, arduino_UNO.D9_PWM
  N9: TFT_1_44_OLEd.pin11, arduino_UNO.D10_PWM/SS
  N10: arduino_UNO.D2, Julien_Deantoni_2019.IN1

notes:
  the schematic is wrong but the breadboard and the PCB ok

custom parts:
  Adafruit MAX31856 Thermocouple Amp: Thermocouples are very sensitive, requiring a good amplifier with a cold-compensation reference, as well as calculations to handle any non-linearities. For a long time we've suggested our MAX31855K breakout, which works great but is only for K-type thermocouples. Now we're happy to offer a great new thermocouple amplifier/converter that can handle just about any type of thermocouple, and even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
  2-Channel 5v Relay Shield: 2 Channel 5v Relay Shield w. 2x SPD-06VDC-SD-C
