# Fritzing sketch kilRegulator_controlerSchematic_v4_arduinoNano_pi3B (saved by Fritzing 0.9.3b)
circuit board: 6.45781cm x 5.61762cm
breadboards: 1

parts:
  Screen_(bottom_side) = IC, SIP package, 11 pins [chip_label="TFT 1.44\" OLED"]
  Q3 = NPN-Transistor [package="SOT-23 [SMD]"]
  D1 = Rectifier Diode [part_number=1N4001 package="300 mil [THT]"]
  R1 = Resistor [tolerance=±5% resistance=220 package=THT]
  R2 = Resistor [tolerance=±5% resistance=220 part_number=fake package=THT]
  JP1 = Header 2 [package=screwterminal-3.5mm-2_lock]
  arduino = Arduino Nano (Rev3.0)
  relay = songle relay
  Max31856 = Adafruit MAX31856 Thermocouple Amp [part_number="Adafruit #3263"]

nets:
  5V: Screen_(bottom_side).pin1, Screen_(bottom_side).pin6, D1.cathode, arduino.5V, relay.VCC, Max31856.VIN
  GND: Screen_(bottom_side).pin3, Q3.2, arduino.GND, Max31856.GND
  N1: Screen_(bottom_side).pin7, arduino.D13/SCK
  N2: Screen_(bottom_side).pin8, arduino.D11/MOSI
  N3: Screen_(bottom_side).pin9, arduino.D8
  N4: Screen_(bottom_side).pin10, arduino.D9
  N5: Screen_(bottom_side).pin11, arduino.D10
  N6: Q3.0, R1.Pin_0
  N7: Q3.1, D1.anode, relay.GND
  N8: R1.Pin_1, arduino.D2
  N9: R2.Pin_0, R2.Pin_1
  N10: JP1.1, relay.COMMON
  N11: JP1.2, relay.NO
  N12: arduino.D3, Max31856.SCK
  N13: arduino.D4, Max31856.SDI
  N14: arduino.D5, Max31856.SDO
  N15: arduino.D7, Max31856.!CS

notes:
  Warning the Screen is on the opposite side of the other components
  Deantoni
  2019
  Julien

custom parts:
  Adafruit MAX31856 Thermocouple Amp: Thermocouples are very sensitive, requiring a good amplifier with a cold-compensation reference, as well as calculations to handle any non-linearities. For a long time we've suggested our MAX31855K breakout, which works great but is only for K-type thermocouples. Now we're happy to offer a great new thermocouple amplifier/converter that can handle just about any type of thermocouple, and even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
