# Fritzing sketch kilRegulator_controlerSchematic_v4_arduinoNano_pizero (saved by Fritzing 0.9.3b)
circuit board: 6.47062cm x 5.72647cm
breadboards: 1

parts:
  Max31856 = Adafruit MAX31856 Thermocouple Amp [part_number="Adafruit #3263"]
  Screen_(bottom_side) = IC, SIP package, 11 pins [chip_label="TFT 1.44\" OLED"]
  relay = songle relay
  Q3 = NPN-Transistor [package="SOT-23 [SMD]"]
  D1 = Rectifier Diode [part_number=1N4001 package="300 mil [THT]"]
  R1 = Resistor [tolerance=±5% resistance=220 package=THT]
  R2 = Resistor [tolerance=±5% resistance=220 part_number=fake package=THT]
  JP1 = Header 2 [package=screwterminal-3.5mm-2_lock]
  arduino = Arduino Nano (Rev3.0)

nets:
  N1: Max31856.!CS, arduino.D7
  N2: Max31856.SDI, arduino.D4
  N3: Max31856.SDO, arduino.D5
  N4: Max31856.SCK, arduino.D3
  GND: Max31856.GND, Screen_(bottom_side).pin3, Q3.2, arduino.GND
  VIN: Max31856.VIN, Screen_(bottom_side).pin1, Screen_(bottom_side).pin6, relay.VCC, D1.cathode
  N5: Screen_(bottom_side).pin7, arduino.D13/SCK
  N6: Screen_(bottom_side).pin8, arduino.D11/MOSI
  N7: Screen_(bottom_side).pin9, arduino.D8
  N8: Screen_(bottom_side).pin10, arduino.D9
  N9: Screen_(bottom_side).pin11, arduino.D10
  N10: relay.NO, JP1.2
  N11: relay.COMMON, JP1.1
  N12: relay.GND, Q3.1, D1.anode
  N13: Q3.0, R1.Pin_0
  N14: R1.Pin_1, arduino.D2
  N15: R2.Pin_0, R2.Pin_1

notes:
  Warning the Screen is on the opposite side of the other components
  Julien
  Deantoni
  2019

custom parts:
  Adafruit MAX31856 Thermocouple Amp: Thermocouples are very sensitive, requiring a good amplifier with a cold-compensation reference, as well as calculations to handle any non-linearities. For a long time we've suggested our MAX31855K breakout, which works great but is only for K-type thermocouples. Now we're happy to offer a great new thermocouple amplifier/converter that can handle just about any type of thermocouple, and even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
