# Fritzing sketch max31856 (saved by Fritzing 0.9.3b)
breadboards: 1

parts:
  Part1 = Adafruit MAX31856 Thermocouple Amp [part_number="Adafruit #3263"]
  Part2 = Arduino Uno (Rev3)

nets:
  N1: Part1.!CS, Part2.D10_PWM/SS
  N2: Part1.SDI, Part2.D11_PWM/MOSI
  N3: Part1.SDO, Part2.D12/MISO
  N4: Part1.SCK, Part2.D13/SCK
  GND: Part1.GND, Part2.GND
  VIN: Part1.VIN, Part2.5V

custom parts:
  Adafruit MAX31856 Thermocouple Amp: Thermocouples are very sensitive, requiring a good amplifier with a cold-compensation reference, as well as calculations to handle any non-linearities. For a long time we've suggested our MAX31855K breakout, which works great but is only for K-type thermocouples. Now we're happy to offer a great new thermocouple amplifier/converter that can handle just about any type of thermocouple, and even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
